// Logisim project Controlador.circ as structural Verilog: 1 circuit, main circuit main
// 8
module main (
  input  in_1,
  input  in_2,
  input  in_3,
  input  in_4,
  input  in_5,
  input  [7:0] PC,
  input  [7:0] Endereco,
  input  in_8,
  input  in_9,
  input  PEGA_PC,
  input  PEGA_IR,
  input  PEGA_IR_2
);

  wire not_1_out, Pega, undriven;
  wire [0:0] and_1_out;
  wire [7:0] \Endereço , \Instrução , IREnd;
  wire [15:0] AEnd, demultiplexer_1_out1, IrIN, ram_1_data, Valor;

  // Probe on IrIN
  or or_1 (Pega, PEGA_PC, PEGA_IR);
  Register #(.width(16)) register_1 (.D(IrIN), .en(in_3), .Q({IREnd, \Instrução }), .clk(in_4), .clr(in_5));
  and and_1 (and_1_out[0], PEGA_IR, not_1_out);
  not not_1 (not_1_out, PEGA_PC);
  Multiplexer #(.select(2), .width(8), .enable("false")) multiplexer_1 (
    .in0(PC), .in1(IREnd), .in2(Endereco), .out(\Endereço ), .sel({PEGA_IR_2, and_1_out[0]}));  // open: in3
  // Probe on \Endereço 
  Demultiplexer #(.width(16), .enable("false")) demultiplexer_1 (
    .out0(IrIN), .out1(demultiplexer_1_out1), .in(Valor), .sel(and_1_out[0]));
  // Probe on undriven
  // Probe on demultiplexer_1_out1
  RAM #(.dataWidth(16)) ram_1 (.addr(\Endereço ), .data(ram_1_data), .sel(1'b1), .clk(in_1), .ld(Pega), .clr(in_2));
  Transistor #(.\type ("n"), .width(16)) transistor_1 (.in(AEnd), .out(ram_1_data), .gate(PEGA_IR_2));
  Transistor #(.\type ("n"), .width(16)) transistor_2 (.in(ram_1_data), .out(Valor), .gate(Pega));
  Register #(.width(16)) register_2 (.D(demultiplexer_1_out1), .en(1'b1), .Q(AEnd), .clk(in_8), .clr(in_9));
  // Probe on ram_1_data

  // Other names for the same wires on the sheet: STA = PEGA_IR_2
endmodule
