// Logisim project controlador.circ as structural Verilog: 1 circuit, main circuit main
module main (
  input  CLOCK,
  input  RESET,
  input  [7:0] PC,
  input  [15:0] ACC_OUT,
  input  [15:0] IR_OUT,
  input  [15:0] RAM_OUT,
  input  [15:0] INN,
  output [7:0] PC_SET,
  output PC_plus_plus,
  output [15:0] ACC_IN,
  output [15:0] IR_IN,
  output [15:0] RAM_IN,
  output [7:0] RAM_ADDR,
  output [15:0] OUT,
  output RAM_CLOCK,
  output READ_ENABLE,
  output PC_ENABLE,
  output ACC_ENABLE,
  output IR_ENABLE
);

  wire and_1_out, CONTA, INN_t, JDZ, JEQ, JGE, JGT, JLE, JLT, JMP, main_4_out_5, main_4_out_8, main_4_out_9,
       main_4_out_10, main_4_out_15, not_1_out, or_1_out, PRN, RAM_CLOCK_t, STA, STOP;
  wire [1:0] counter_1_q;
  wire [2:0] main_2_out_3;
  wire [15:0] OUT_MEM;

  Demultiplexer #(.select(2), .width(16), .enable("false")) demultiplexer_1 (
    .out0(IR_IN), .out1(ACC_IN), .out2(OUT_MEM), .in(RAM_OUT), .sel({PRN, STA}));  // open: out3
  Multiplexer #(.width(8), .enable("false")) multiplexer_1 (
    .in0(PC), .in1(IR_OUT[7:0]), .out(RAM_ADDR), .sel(not_1_out));
  not not_1 (not_1_out, IR_ENABLE);
  Multiplexer #(.width(16), .enable("false")) multiplexer_2 (.in0(INN), .in1(ACC_OUT), .out(RAM_IN), .sel(STA));
  not not_2 (RAM_CLOCK, RAM_CLOCK_t);
  Jumpador_main main_1 (
    .JMP(JMP), .JLE(JLE), .JDZ(JDZ), .JGT(JGT), .JEQ(JEQ), .JLT(JLT), .JGE(JGE), .PC_ENABLE(PC_ENABLE),
    .in_8(ACC_OUT));
  or or_1 (or_1_out, STA, INN_t);
  not not_3 (READ_ENABLE, or_1_out);
  Counter #(.width(2), .max('h2)) counter_1 (
    .Q(counter_1_q), .clk(and_1_out), .clr(RESET));  // open: load, D, count, carry
  and and_1 (and_1_out, CLOCK, ~STOP);  // AND_Gate
  tradutor_main main_2 (.in_2(IR_OUT[15:8]), .out_3(main_2_out_3), .in_1(CONTA));
  Demultiplexer #(.select(2), .enable("false")) demultiplexer_2 (
    .out0(IR_ENABLE), .out1(RAM_CLOCK_t), .out2(PC_plus_plus), .in(1'b1), .sel(counter_1_q));  // open: out3
  Register #(.width(16)) register_1 (.D(OUT_MEM), .en(PRN), .Q(OUT), .clk(RAM_CLOCK_t));  // open: clr
  IF_main main_3 (
    .out_3(ACC_ENABLE), .out_7(JMP), .STA(STA), .out_5(STOP), .in_1(IR_OUT[15:8]), .in_2(RAM_CLOCK_t));  // open: out_6
  IFao_main main_4 (
    .out_13(PRN), .out_12(INN_t), .out_7(JGE), .out_3(JLT), .out_11(JEQ), .out_14(JGT), .out_4(JDZ),
    .out_6(JLE), .out_5(main_4_out_5), .out_8(main_4_out_8), .out_10(main_4_out_10), .out_15(main_4_out_15),
    .out_9(main_4_out_9), .in_2(RAM_CLOCK_t), .in_1(IR_OUT[15:8]));
  or or_2 (CONTA, main_4_out_10, main_4_out_9, main_4_out_15, main_4_out_8, main_4_out_5);

  assign PC_SET = IR_OUT[7:0];

  // Other names for the same wires on the sheet: IN[15:0] = INN; IR_ADDR[7:0] = IR_OUT[7:0];
  //   IR_INST[7:0] = IR_OUT[15:8]; LDA = ACC_ENABLE; PEGA_PC = IR_ENABLE

  // Notes on the sheet:
  //   ULA
endmodule
